# Fritzing sketch 201902_GameBoard_fudged_final1_grounded_named (saved by Fritzing 0.9.3b)
circuit board: 17.5cm x 13cm
breadboards: 1

parts:
  Quarz_16MHz = Crystal [frequency="16 Mhz" package=THT]
  Atmega328p = atmega328p [package=dip]
  Reset_1kR = Resistor [tolerance=±5% resistance=1k package=THT]
  SPI = AVR ISP 6 Pin [package=2x3_lock]
  SR-1 = 74HC595 [package="DIP16 [THT]"]
  Periph_1kR = Resistor [tolerance=±5% resistance=1k package=THT]
  2N2222 = TRANSISTOR_NPN [package=to-92-ammo]
  SR-2 = 74HC595 [package="DIP16 [THT]"]
  SR-3 = 74HC595 [package="DIP16 [THT]"]
  SR-4 = 74HC595 [package="DIP16 [THT]"]
  pIn-1 = 74HC165 [package="DIP16 [THT]"]
  pIn-2 = 74HC165 [package="DIP16 [THT]"]
  pIn-3 = 74HC165 [package="DIP16 [THT]"]
  pIn-4 = 74HC165 [package="DIP16 [THT]"]
  latch-1 = CD4043B [package="DIP16 [THT]"]
  latch-2 = CD4043B [package="DIP16 [THT]"]
  latch-4 = CD4043B [package="DIP16 [THT]"]
  latch-5 = CD4043B [package="DIP16 [THT]"]
  latch-6 = CD4043B [package="DIP16 [THT]"]
  latch-7 = CD4043B [package="DIP16 [THT]"]
  latch-8 = CD4043B [package="DIP16 [THT]"]
  R-OnOff = Resistor [tolerance=±5% resistance=1k package=THT]
  C1_22nF = Capacitor [package=cap-pth-small2]
  C2_22nF = Capacitor [package=cap-pth-small2]
  R1 = Resistor [tolerance=±5% resistance=1k package=THT]
  R2 = Resistor [tolerance=±5% resistance=1k package=THT]
  R3 = Resistor [tolerance=±5% resistance=1k package=THT]
  R4 = Resistor [tolerance=±5% resistance=1k package=THT]
  R5 = Resistor [tolerance=±5% resistance=1k package=THT]
  R8 = Resistor [tolerance=±5% resistance=1k package=THT]
  R7 = Resistor [tolerance=±5% resistance=1k package=THT]
  R6 = Resistor [tolerance=±5% resistance=1k package=THT]
  R9 = Resistor [tolerance=±5% resistance=1k package=THT]
  R13 = Resistor [tolerance=±5% resistance=1k package=THT]
  R11 = Resistor [tolerance=±5% resistance=1k package=THT]
  R15 = Resistor [tolerance=±5% resistance=1k package=THT]
  R16 = Resistor [tolerance=±5% resistance=1k package=THT]
  R14 = Resistor [tolerance=±5% resistance=1k package=THT]
  R10 = Resistor [tolerance=±5% resistance=1k package=THT]
  R12 = Resistor [tolerance=±5% resistance=1k package=THT]
  R17 = Resistor [tolerance=±5% resistance=1k package=THT]
  R23 = Resistor [tolerance=±5% resistance=1k package=THT]
  R18 = Resistor [tolerance=±5% resistance=1k package=THT]
  R19 = Resistor [tolerance=±5% resistance=1k package=THT]
  R20 = Resistor [tolerance=±5% resistance=1k package=THT]
  R24 = Resistor [tolerance=±5% resistance=1k package=THT]
  R21 = Resistor [tolerance=±5% resistance=1k package=THT]
  R22 = Resistor [tolerance=±5% resistance=1k package=THT]
  R27 = Resistor [tolerance=±5% resistance=1k package=THT]
  R29 = Resistor [tolerance=±5% resistance=1k package=THT]
  R25 = Resistor [tolerance=±5% resistance=1k package=THT]
  R28 = Resistor [tolerance=±5% resistance=1k package=THT]
  R26 = Resistor [tolerance=±5% resistance=1k package=THT]
  R30 = Resistor [tolerance=±5% resistance=1k package=THT]
  1kR = Resistor [tolerance=±5% resistance=1k package=THT]
  R31 = Resistor [tolerance=±5% resistance=1k package=THT]
  PinOut1 = 8-pin connector [package=1x08]
  PinOut2 = 8-pin connector [package=1x08]
  PinOut3 = 8-pin connector [package=1x08]
  PinOut4 = 8-pin connector [package=1x08]
  PinIn1 = 8-pin connector [package=1x08]
  PinIn2 = 8-pin connector [package=1x08]
  PinIn3 = 8-pin connector [package=1x08]
  PinIn4 = 8-pin connector [package=1x08]
  Output_pins = 8-pin connector [package=1x08]
  GND_D7_B1-B3_VCC = 8-pin connector [package=1x08]
  Button_Matrix = Pad [width=1.5 height=1.5 connect=center]
  J8 = female pin header, 2 pins [form="♀ (female)"]
  J7 = female pin header, 2 pins [form="♀ (female)"]
  J3 = female pin header, 2 pins [form="♀ (female)"]
  J4 = female pin header, 2 pins [form="♀ (female)"]
  J5 = female pin header, 2 pins [form="♀ (female)"]
  J6 = female pin header, 2 pins [form="♀ (female)"]
  E_B_C = female pin header, 2 pins [form="♀ (female)"]
  J2 = female pin header, 2 pins [form="♀ (female)"]
  Pad2 = Pad [width=1.5 height=1.5 connect=center]
  Pad3 = Pad [width=1.5 height=1.5 connect=center]
  Pad4 = Pad [width=1.5 height=1.5 connect=center]
  Pad5 = Pad [width=1.5 height=1.5 connect=center]
  Pad6 = Pad [width=1.5 height=1.5 connect=center]
  Pad7 = Pad [width=1.5 height=1.5 connect=center]
  Pad8 = Pad [width=1.5 height=1.5 connect=center]
  J16 = female pin header, 2 pins [form="♀ (female)"]
  J14 = female pin header, 2 pins [form="♀ (female)"]
  J12 = female pin header, 2 pins [form="♀ (female)"]
  J10 = female pin header, 2 pins [form="♀ (female)"]
  J15 = female pin header, 2 pins [form="♀ (female)"]
  J13 = female pin header, 2 pins [form="♀ (female)"]
  J11 = female pin header, 2 pins [form="♀ (female)"]
  J9 = female pin header, 2 pins [form="♀ (female)"]
  J24 = female pin header, 2 pins [form="♀ (female)"]
  J22 = female pin header, 2 pins [form="♀ (female)"]
  J20 = female pin header, 2 pins [form="♀ (female)"]
  J18 = female pin header, 2 pins [form="♀ (female)"]
  J23 = female pin header, 2 pins [form="♀ (female)"]
  J21 = female pin header, 2 pins [form="♀ (female)"]
  J19 = female pin header, 2 pins [form="♀ (female)"]
  J17 = female pin header, 2 pins [form="♀ (female)"]
  npn = female pin header, 2 pins [form="♀ (female)"]
  J30 = female pin header, 2 pins [form="♀ (female)"]
  J28 = female pin header, 2 pins [form="♀ (female)"]
  J26 = female pin header, 2 pins [form="♀ (female)"]
  J31 = female pin header, 2 pins [form="♀ (female)"]
  J29 = female pin header, 2 pins [form="♀ (female)"]
  J27 = female pin header, 2 pins [form="♀ (female)"]
  J25 = female pin header, 2 pins [form="♀ (female)"]
  Pad9 = Pad [width=1.5 height=1.5 connect=center]
  Pad10 = Pad [width=1.5 height=1.5 connect=center]
  Pad11 = Pad [width=1.5 height=1.5 connect=center]
  Pad12 = Pad [width=1.5 height=1.5 connect=center]
  Pad13 = Pad [width=1.5 height=1.5 connect=center]
  Pad14 = Pad [width=1.5 height=1.5 connect=center]
  Pad15 = Pad [width=1.5 height=1.5 connect=center]
  Pad16 = Pad [width=1.5 height=1.5 connect=center]
  Pad17 = Pad [width=1.5 height=1.5 connect=center]
  Pad18 = Pad [width=1.5 height=1.5 connect=center]
  Pad19 = Pad [width=1.5 height=1.5 connect=center]
  Pad20 = Pad [width=1.5 height=1.5 connect=center]
  Pad21 = Pad [width=1.5 height=1.5 connect=center]
  Pad22 = Pad [width=1.5 height=1.5 connect=center]
  Pad23 = Pad [width=1.5 height=1.5 connect=center]
  Pad24 = Pad [width=1.5 height=1.5 connect=center]
  Pad25 = Pad [width=1.5 height=1.5 connect=center]
  Pad26 = Pad [width=1.5 height=1.5 connect=center]
  Pad27 = Pad [width=1.5 height=1.5 connect=center]
  Pad28 = Pad [width=1.5 height=1.5 connect=center]
  Pad29 = Pad [width=1.5 height=1.5 connect=center]
  Pad30 = Pad [width=1.5 height=1.5 connect=center]
  Pad31 = Pad [width=1.5 height=1.5 connect=center]
  74HC595 = Pad [width=1.5 height=1.5 connect=center]
  Out0 = Pad [width=1.5 height=1.5 connect=center]
  Pad34 = Pad [width=1.5 height=1.5 connect=center]
  Pad35 = Pad [width=1.5 height=1.5 connect=center]
  Pad36 = Pad [width=1.5 height=1.5 connect=center]
  Pad37 = Pad [width=1.5 height=1.5 connect=center]
  Pad38 = Pad [width=1.5 height=1.5 connect=center]
  Pad39 = Pad [width=1.5 height=1.5 connect=center]
  Pad40 = Pad [width=1.5 height=1.5 connect=center]
  Pad41 = Pad [width=1.5 height=1.5 connect=center]
  Pad42 = Pad [width=1.5 height=1.5 connect=center]
  Pad43 = Pad [width=1.5 height=1.5 connect=center]
  Pad44 = Pad [width=1.5 height=1.5 connect=center]
  Pad45 = Pad [width=1.5 height=1.5 connect=center]
  Out31 = Pad [width=1.5 height=1.5 connect=center]
  Pad47 = Pad [width=1.5 height=1.5 connect=center]
  Pad48 = Pad [width=1.5 height=1.5 connect=center]
  VCC = Pad [width=1.939688533849746 height=1.8388509642540376 connect=center]
  GND = Pad [width=1.939688533849746 height=1.8388509642540376 connect=center]
  Pad51 = Pad [width=0.65874852847958409 height=0.72959159648647431 connect=center]
  Pad52 = Pad [width=0.65874852847958409 height=0.72959159648647431 connect=center]
  Pad54 = Pad [width=0.46960137248963946 height=0.52189322837824303 connect=center]
  Pad55 = Pad [width=0.46960137248963946 height=0.52189322837824303 connect=center]
  Pad56 = Pad [width=0.46960137248963946 height=0.52189322837824303 connect=center]
  Pad57 = Pad [width=0.46960137248963946 height=0.52189322837824303 connect=center]
  Pad58 = Pad [width=0.65874852847958409 height=0.72959159648647431 connect=center]
  Pad59 = Pad [width=0.65874852847958409 height=0.72959159648647431 connect=center]
  Pad60 = Pad [width=0.65874852847958409 height=0.72959159648647431 connect=center]
  Pad61 = Pad [width=0.46960137248963946 height=0.52189322837824303 connect=center]
  Pad63 = Pad [width=0.46960137248963946 height=0.52189322837824303 connect=center]
  Pad64 = Pad [width=0.46960137248963946 height=0.52189322837824303 connect=center]
  Pad65 = Pad [width=0.46960137248963946 height=0.52189322837824303 connect=center]
  Pad66 = Pad [width=0.65874852847958409 height=0.72959159648647431 connect=center]
  Pad67 = Pad [width=0.65874852847958409 height=0.72959159648647431 connect=center]
  GND_2 = Pad [width=0.65874852847958409 height=0.72959159648647431 connect=center]
  Pad69 = Pad [width=0.65874852847958409 height=0.72959159648647431 connect=center]
  Pad70 = Pad [width=0.65874852847958409 height=0.72959159648647431 connect=center]
  Pad71 = Pad [width=0.65874852847958409 height=0.72959159648647431 connect=center]
  D0_D1_B0_VCCo_GND = Pad [width=0.65874852847958409 height=0.72959159648647431 connect=center]
  Pad73 = Pad [width=0.65874852847958409 height=0.72959159648647431 connect=center]
  Q7s = female pin header, 1 pin [form="♀ (female)"]
  In0 = Resistor [tolerance=±5% resistance=10k package=THT]
  R34 = Resistor [tolerance=±5% resistance=10k package=THT]
  R35 = Resistor [tolerance=±5% resistance=10k package=THT]
  R36 = Resistor [tolerance=±5% resistance=10k package=THT]
  R37 = Resistor [tolerance=±5% resistance=10k package=THT]
  R40 = Resistor [tolerance=±5% resistance=10k package=THT]
  R38 = Resistor [tolerance=±5% resistance=10k package=THT]
  R39 = Resistor [tolerance=±5% resistance=10k package=THT]
  R41 = Resistor [tolerance=±5% resistance=10k package=THT]
  R45 = Resistor [tolerance=±5% resistance=10k package=THT]
  R48 = Resistor [tolerance=±5% resistance=10k package=THT]
  R47 = Resistor [tolerance=±5% resistance=10k package=THT]
  R44 = Resistor [tolerance=±5% resistance=10k package=THT]
  R43 = Resistor [tolerance=±5% resistance=10k package=THT]
  R42 = Resistor [tolerance=±5% resistance=10k package=THT]
  R46 = Resistor [tolerance=±5% resistance=10k package=THT]
  R49 = Resistor [tolerance=±5% resistance=10k package=THT]
  R53 = Resistor [tolerance=±5% resistance=10k package=THT]
  R56 = Resistor [tolerance=±5% resistance=10k package=THT]
  R55 = Resistor [tolerance=±5% resistance=10k package=THT]
  R52 = Resistor [tolerance=±5% resistance=10k package=THT]
  R51 = Resistor [tolerance=±5% resistance=10k package=THT]
  R50 = Resistor [tolerance=±5% resistance=10k package=THT]
  R54 = Resistor [tolerance=±5% resistance=10k package=THT]
  R57 = Resistor [tolerance=±5% resistance=10k package=THT]
  R61 = Resistor [tolerance=±5% resistance=10k package=THT]
  In31 = Resistor [tolerance=±5% resistance=10k package=THT]
  10kR = Resistor [tolerance=±5% resistance=10k package=THT]
  R60 = Resistor [tolerance=±5% resistance=10k package=THT]
  R59 = Resistor [tolerance=±5% resistance=10k package=THT]
  R58 = Resistor [tolerance=±5% resistance=10k package=THT]
  GND_3 = Resistor [tolerance=±5% resistance=10k package=THT]
  Pad74 = Pad [width=0.46960137248963946 height=0.52189322837824303 connect=center]
  Pad75 = Pad [width=0.46960137248963946 height=0.52189322837824303 connect=center]
  Pad77 = Pad [width=0.46960137248963946 height=0.52189322837824303 connect=center]
  Pad80 = Pad [width=0.46960137248963946 height=0.52189322837824303 connect=center]
  Pad81 = Pad [width=0.46960137248963946 height=0.52189322837824303 connect=center]
  latch-3 = CD4043B [package="DIP16 [THT]"]
  Pad84 = Pad [width=0.46960137248963946 height=0.52189322837824303 connect=center]
  Pad85 = Pad [width=0.46960137248963946 height=0.52189322837824303 connect=center]
  Pad86 = Pad [width=0.46960137248963946 height=0.52189322837824303 connect=center]
  Pad89 = Pad [width=0.46960137248963946 height=0.52189322837824303 connect=center]
  Pad90 = Pad [width=0.46960137248963946 height=0.52189322837824303 connect=center]
  Pad91 = Pad [width=0.46960137248963946 height=0.52189322837824303 connect=center]
  Pad92 = Pad [width=0.46960137248963946 height=0.52189322837824303 connect=center]
  Pad94 = Pad [width=0.65874852847958409 height=0.72959159648647431 connect=center]
  Pad95 = Pad [width=0.65874852847958409 height=0.72959159648647431 connect=center]
  Pad96 = Pad [width=0.65874852847958409 height=0.72959159648647431 connect=center]
  Pad97 = Pad [width=0.65874852847958409 height=0.72959159648647431 connect=center]
  Pad98 = Pad [width=0.65874852847958409 height=0.72959159648647431 connect=center]
  Pad99 = Pad [width=0.65874852847958409 height=0.72959159648647431 connect=center]
  Pad100 = Pad [width=0.65874852847958409 height=0.72959159648647431 connect=center]
  Pad101 = Pad [width=0.65874852847958409 height=0.72959159648647431 connect=center]
  Pad102 = Pad [width=0.65874852847958409 height=0.72959159648647431 connect=center]
  Pad103 = Pad [width=0.65874852847958409 height=0.72959159648647431 connect=center]
  Pad104 = Pad [width=0.65874852847958409 height=0.72959159648647431 connect=center]
  Pad105 = Pad [width=0.65874852847958409 height=0.72959159648647431 connect=center]
  Pad106 = Pad [width=0.65874852847958409 height=0.72959159648647431 connect=center]
  Pad107 = Pad [width=0.65874852847958409 height=0.72959159648647431 connect=center]
  Pad108 = Pad [width=0.65874852847958409 height=0.72959159648647431 connect=center]
  Pad109 = Pad [width=0.65874852847958409 height=0.72959159648647431 connect=center]
  Pad110 = Pad [width=0.65874852847958409 height=0.72959159648647431 connect=center]
  Pad112 = Pad [width=0.46960137248963946 height=0.52189322837824303 connect=center]
  Pad113 = Pad [width=0.46960137248963946 height=0.52189322837824303 connect=center]
  Pad114 = Pad [width=0.46960137248963946 height=0.52189322837824303 connect=center]
  Pad115 = Pad [width=0.46960137248963946 height=0.52189322837824303 connect=center]
  Pad116 = Pad [width=0.46960137248963946 height=0.52189322837824303 connect=center]
  Pad117 = Pad [width=0.46960137248963946 height=0.52189322837824303 connect=center]
  Pad118 = Pad [width=0.46960137248963946 height=0.52189322837824303 connect=center]
  ©_Johannes_Wilde = Pad [width=0.65874852847958409 height=0.72959159648647431 connect=center]
  Pad122 = Pad [width=0.65874852847958409 height=0.72959159648647431 connect=center]
  Revision_1 = Pad [width=0.65874852847958409 height=0.72959159648647431 connect=center]
  Pad124 = Pad [width=0.46960137248963946 height=0.52189322837824303 connect=center]
  Pad125 = Pad [width=0.46960137248963946 height=0.52189322837824303 connect=center]
  Pad126 = Pad [width=0.46960137248963946 height=0.52189322837824303 connect=center]
  Pad127 = Pad [width=0.46960137248963946 height=0.52189322837824303 connect=center]
  Pad128 = Pad [width=0.65874852847958409 height=0.72959159648647431 connect=center]
  Pad129 = Pad [width=0.65874852847958409 height=0.72959159648647431 connect=center]
  Pad130 = Pad [width=0.65874852847958409 height=0.72959159648647431 connect=center]
  74HC165 = Pad [width=0.65874852847958409 height=0.72959159648647431 connect=center]
  CD4043B = Pad [width=0.65874852847958409 height=0.72959159648647431 connect=center]
  Pad133 = Pad [width=0.65874852847958409 height=0.72959159648647431 connect=center]
  C3_220uF = Electrolytic Capacitor [capacitance=0.22mF package="200 mil [THT, electrolytic]"]
  C4_220uF = Electrolytic Capacitor [capacitance=0.22mF package="200 mil [THT, electrolytic]"]
  USB-Power = Mini-USB _B_ connector with 5th pin broken out. [package=usb-minib]
  VCC_2 = Pad [width=0.65874852847958409 height=0.72959159648647431 connect=center]
  March_2019 = Pad [width=0.65874852847958409 height=0.72959159648647431 connect=center]

nets:
  N1: Quarz_16MHz.pin_0, Atmega328p.B6_(XTAL1), C1_22nF.1
  N2: Quarz_16MHz.pin_1, Atmega328p.B7_(XTAL2), C2_22nF.1
  N3: Atmega328p.RESET, Reset_1kR.Pin_1, SPI.5
  N4: Atmega328p.D0_(RX), Output_pins.7
  N5: Atmega328p.D1_(TX), Output_pins.6
  N6: Atmega328p.D2, SR-1.DS
  N7: Atmega328p.D3_(PWM), SR-1.OE, SR-2.OE, SR-3.OE, SR-4.OE, Pad54.pad, Pad55.pad, Pad56.pad, Pad57.pad, Pad61.pad, Pad63.pad, Pad64.pad, Pad65.pad
  N8: Atmega328p.D4, SR-1.ST_CP, SR-2.ST_CP, SR-3.ST_CP, SR-4.ST_CP, Pad51.pad, Pad52.pad, Pad66.pad, Pad67.pad, GND_2.pad, Pad69.pad, Pad70.pad, Pad71.pad
  5V: Atmega328p.VCC, Atmega328p.AVCC, Atmega328p.AREF, Reset_1kR.Pin_0, SPI.2, 2N2222.C, GND_D7_B1-B3_VCC.0, GND_D7_B1-B3_VCC.1, Button_Matrix.pad, Pad2.pad, Pad3.pad, Pad4.pad, Pad5.pad, Pad6.pad, Pad7.pad, Pad8.pad, Pad9.pad, Pad10.pad, Pad11.pad, Pad12.pad, Pad13.pad, Pad14.pad, Pad15.pad, Pad16.pad, Pad17.pad, Pad18.pad, Pad19.pad, Pad20.pad, Pad21.pad, Pad22.pad, Pad23.pad, Pad24.pad, Pad25.pad, Pad26.pad, Pad27.pad, Pad28.pad, Pad29.pad, Pad30.pad, Pad31.pad, 74HC595.pad, Out0.pad, Pad34.pad, Pad35.pad, Pad36.pad, Pad37.pad, Pad38.pad, Pad39.pad, Pad40.pad, Pad41.pad, Pad42.pad, Pad43.pad, Pad44.pad, Pad45.pad, Out31.pad, Pad47.pad, Pad48.pad, VCC.pad, Pad112.pad, Pad113.pad, Pad124.pad, Pad125.pad, Pad126.pad, Pad127.pad, C3_220uF.+, C4_220uF.+, USB-Power.VBUS, VCC_2.pad, March_2019.pad
  GND: Atmega328p.GND, SPI.6, SR-1.GND, SR-2.GND, SR-3.GND, SR-4.GND, pIn-1.GND, pIn-1.Q0, pIn-2.GND, pIn-2.Q0, pIn-3.GND, pIn-3.Q0, pIn-4.GND, pIn-4.MR, pIn-4.Q0, latch-1.GND, latch-2.GND, latch-4.GND, latch-5.GND, latch-6.GND, latch-7.GND, latch-8.GND, C1_22nF.2, C2_22nF.2, Output_pins.0, Output_pins.1, Output_pins.4, GND_D7_B1-B3_VCC.6, GND_D7_B1-B3_VCC.7, GND.pad, D0_D1_B0_VCCo_GND.pad, Pad73.pad, In0.Pin_1, R34.Pin_1, R35.Pin_1, R36.Pin_1, R37.Pin_1, R40.Pin_1, R38.Pin_1, R39.Pin_1, R41.Pin_1, R45.Pin_1, R48.Pin_1, R47.Pin_1, R44.Pin_1, R43.Pin_1, R42.Pin_1, R46.Pin_1, R49.Pin_1, R53.Pin_1, R56.Pin_1, R55.Pin_1, R52.Pin_1, R51.Pin_1, R50.Pin_1, R54.Pin_1, R57.Pin_1, R61.Pin_1, In31.Pin_1, 10kR.Pin_1, R60.Pin_1, R59.Pin_1, R58.Pin_1, GND_3.Pin_1, latch-3.GND, Pad94.pad, Pad95.pad, Pad96.pad, Pad97.pad, Pad98.pad, Pad99.pad, Pad100.pad, Pad101.pad, Pad102.pad, Pad103.pad, Pad104.pad, Pad105.pad, Pad106.pad, Pad107.pad, Pad108.pad, Pad109.pad, Pad110.pad, ©_Johannes_Wilde.pad, Pad122.pad, Revision_1.pad, Pad128.pad, Pad129.pad, Pad130.pad, 74HC165.pad, CD4043B.pad, Pad133.pad, C3_220uF.-, C4_220uF.-, USB-Power.MTN2, USB-Power.MTN3, USB-Power.MTN1, USB-Power.MTN4, USB-Power.GND
  N9: Atmega328p.D5_(PWM), SR-1.SH_CP, SR-2.SH_CP, SR-3.SH_CP, SR-4.SH_CP
  N10: Atmega328p.D6_(PWM), SR-1.MR, SR-2.MR, SR-3.MR, SR-4.MR, Pad58.pad, Pad59.pad, Pad60.pad
  N11: Atmega328p.D7, GND_D7_B1-B3_VCC.5
  N12: Atmega328p.B0, R-OnOff.Pin_1
  N13: Atmega328p.B1_(PWM), GND_D7_B1-B3_VCC.4
  N14: Atmega328p.B2_(PWM), GND_D7_B1-B3_VCC.3
  N15: Atmega328p.B3_(PWM), SPI.4
  N16: Atmega328p.B4, SPI.1
  N17: Atmega328p.B5, SPI.3
  N18: Atmega328p.C0, GND_D7_B1-B3_VCC.2
  N19: Atmega328p.C1, latch-1.Q3, latch-1.Q7, latch-1.SH_CP, latch-1.Q0, latch-2.Q3, latch-2.Q7, latch-2.SH_CP, latch-2.Q0, latch-4.Q3, latch-4.Q7, latch-4.SH_CP, latch-4.Q0, latch-5.Q3, latch-5.Q7, latch-5.SH_CP, latch-5.Q0, latch-6.Q7, latch-6.SH_CP, latch-6.Q0, latch-7.Q7, latch-7.SH_CP, latch-7.Q0, latch-8.Q7, latch-8.SH_CP, latch-8.Q0, latch-3.Q3, latch-3.Q7, latch-3.SH_CP, latch-3.Q0
  N20: Atmega328p.C2, pIn-1.Q2, pIn-2.Q2, pIn-3.Q2, pIn-4.Q2
  N21: Atmega328p.C3, pIn-1.Q1, pIn-2.Q1, pIn-3.Q1, pIn-4.Q1
  N22: Atmega328p.C4, pIn-1.Q7'
  N23: Atmega328p.C5, Periph_1kR.Pin_0
  N24: SR-1.Q1, R2.Pin_1
  N25: SR-1.Q2, R3.Pin_1
  N26: SR-1.Q3, R4.Pin_1
  N27: SR-1.Q4, R5.Pin_1
  N28: SR-1.Q5, R6.Pin_1
  N29: SR-1.Q6, R7.Pin_1
  N30: SR-1.Q7, R8.Pin_1
  N31: SR-1.Q7', SR-2.DS
  N32: SR-1.Q0, R1.Pin_1
  VCC: SR-1.VCC, 2N2222.E, SR-2.VCC, SR-3.VCC, SR-4.VCC, pIn-1.VCC, pIn-2.VCC, pIn-3.VCC, pIn-4.VCC, latch-1.Q5, latch-1.VCC, latch-2.Q5, latch-2.VCC, latch-4.Q5, latch-4.VCC, latch-5.Q5, latch-5.VCC, latch-6.Q5, latch-6.VCC, latch-7.Q5, latch-7.VCC, latch-8.Q5, latch-8.VCC, Output_pins.2, Output_pins.3, Pad74.pad, Pad75.pad, Pad77.pad, Pad80.pad, Pad81.pad, latch-3.Q5, latch-3.VCC, Pad84.pad, Pad85.pad, Pad86.pad, Pad89.pad, Pad90.pad, Pad91.pad, Pad92.pad, Pad114.pad, Pad115.pad, Pad116.pad, Pad117.pad, Pad118.pad
  N33: Periph_1kR.Pin_1, 2N2222.B
  N34: SR-2.Q1, R10.Pin_1
  N35: SR-2.Q2, R11.Pin_1
  N36: SR-2.Q3, R12.Pin_1
  N37: SR-2.Q4, R13.Pin_1
  N38: SR-2.Q5, R14.Pin_1
  N39: SR-2.Q6, R15.Pin_1
  N40: SR-2.Q7, R16.Pin_1
  N41: SR-2.Q7', SR-3.DS
  N42: SR-2.Q0, R9.Pin_1
  N43: SR-3.Q1, R18.Pin_1
  N44: SR-3.Q2, R19.Pin_1
  N45: SR-3.Q3, R20.Pin_1
  N46: SR-3.Q4, R21.Pin_1
  N47: SR-3.Q5, R22.Pin_1
  N48: SR-3.Q6, R23.Pin_1
  N49: SR-3.Q7, R24.Pin_1
  N50: SR-3.Q7', SR-4.DS
  N51: SR-3.Q0, R17.Pin_1
  N52: SR-4.Q1, R26.Pin_1
  N53: SR-4.Q2, R27.Pin_1
  N54: SR-4.Q3, R28.Pin_1
  N55: SR-4.Q4, R29.Pin_1
  N56: SR-4.Q5, R30.Pin_1
  N57: SR-4.Q6, R31.Pin_1
  N58: SR-4.Q7, 1kR.Pin_1
  N59: SR-4.Q7', Q7s.pin1
  N60: SR-4.Q0, R25.Pin_1
  N61: pIn-1.Q3, latch-2.Q2
  N62: pIn-1.Q4, latch-2.Q7'
  N63: pIn-1.Q5, latch-2.Q1
  N64: pIn-1.Q6, latch-2.MR
  N65: pIn-1.MR, pIn-2.Q7'
  N66: pIn-1.SH_CP, latch-1.MR
  N67: pIn-1.ST_CP, latch-1.Q1
  N68: pIn-1.OE, latch-1.Q7'
  N69: pIn-1.DS, latch-1.Q2
  N70: pIn-2.Q3, latch-4.Q2
  N71: pIn-2.Q4, latch-4.Q7'
  N72: pIn-2.Q5, latch-4.Q1
  N73: pIn-2.Q6, latch-4.MR
  N74: pIn-2.MR, pIn-3.Q7'
  N75: pIn-2.SH_CP, latch-3.MR
  N76: pIn-2.ST_CP, latch-3.Q1
  N77: pIn-2.OE, latch-3.Q7'
  N78: pIn-2.DS, latch-3.Q2
  N79: pIn-3.Q3, latch-6.Q2
  N80: pIn-3.Q4, latch-6.Q7'
  N81: pIn-3.Q5, latch-6.Q1
  N82: pIn-3.Q6, latch-6.MR
  N83: pIn-3.MR, pIn-4.Q7'
  N84: pIn-3.SH_CP, latch-5.MR
  N85: pIn-3.ST_CP, latch-5.Q1
  N86: pIn-3.OE, latch-5.Q7'
  N87: pIn-3.DS, latch-5.Q2
  N88: pIn-4.Q3, latch-8.Q2
  N89: pIn-4.Q4, latch-8.Q7'
  N90: pIn-4.Q5, latch-8.Q1
  N91: pIn-4.Q6, latch-8.MR
  N92: pIn-4.SH_CP, latch-7.MR
  N93: pIn-4.ST_CP, latch-7.Q1
  N94: pIn-4.OE, latch-7.Q7'
  N95: pIn-4.DS, latch-7.Q2
  N96: latch-1.Q4, PinIn1.0, In0.Pin_0
  N97: latch-1.Q6, PinIn1.1, R34.Pin_0
  N98: latch-1.ST_CP, PinIn1.3, R36.Pin_0
  N99: latch-1.DS, PinIn1.2, R35.Pin_0
  N100: latch-2.Q4, PinIn1.4, R37.Pin_0
  N101: latch-2.Q6, PinIn1.5, R38.Pin_0
  N102: latch-2.ST_CP, PinIn1.7, R40.Pin_0
  N103: latch-2.DS, PinIn1.6, R39.Pin_0
  N104: latch-4.Q4, PinIn2.4, R45.Pin_0
  N105: latch-4.Q6, PinIn2.5, R46.Pin_0
  N106: latch-4.ST_CP, PinIn2.7, R48.Pin_0
  N107: latch-4.DS, PinIn2.6, R47.Pin_0
  N108: latch-5.Q4, PinIn3.0, R49.Pin_0
  N109: latch-5.Q6, PinIn3.1, R50.Pin_0
  N110: latch-5.ST_CP, PinIn3.3, R52.Pin_0
  N111: latch-5.DS, PinIn3.2, R51.Pin_0
  N112: latch-6.Q4, PinIn3.4, R53.Pin_0
  N113: latch-6.Q6, PinIn3.5, R54.Pin_0
  N114: latch-6.ST_CP, PinIn3.7, R56.Pin_0
  N115: latch-6.DS, PinIn3.6, R55.Pin_0
  N116: latch-7.Q4, PinIn4.0, R57.Pin_0
  N117: latch-7.Q6, PinIn4.1, R58.Pin_0
  N118: latch-7.ST_CP, PinIn4.3, R60.Pin_0
  N119: latch-7.DS, PinIn4.2, R59.Pin_0
  N120: latch-8.Q4, PinIn4.4, R61.Pin_0
  N121: latch-8.Q6, PinIn4.5, GND_3.Pin_0
  N122: latch-8.ST_CP, PinIn4.7, In31.Pin_0
  N123: latch-8.DS, PinIn4.6, 10kR.Pin_0
  N124: R-OnOff.Pin_0, Output_pins.5
  N125: R1.Pin_0, E_B_C.pin1
  N126: R2.Pin_0, J2.pin1
  N127: R3.Pin_0, J3.pin1
  N128: R4.Pin_0, J4.pin1
  N129: R5.Pin_0, J5.pin1
  N130: R8.Pin_0, J8.pin1
  N131: R7.Pin_0, J7.pin1
  N132: R6.Pin_0, J6.pin1
  N133: R9.Pin_0, J9.pin1
  N134: R13.Pin_0, J13.pin1
  N135: R11.Pin_0, J11.pin1
  N136: R15.Pin_0, J15.pin1
  N137: R16.Pin_0, J16.pin1
  N138: R14.Pin_0, J14.pin1
  N139: R10.Pin_0, J10.pin1
  N140: R12.Pin_0, J12.pin1
  N141: R17.Pin_0, J17.pin1
  N142: R23.Pin_0, J23.pin1
  N143: R18.Pin_0, J18.pin1
  N144: R19.Pin_0, J19.pin1
  N145: R20.Pin_0, J20.pin1
  N146: R24.Pin_0, J24.pin1
  N147: R21.Pin_0, J21.pin1
  N148: R22.Pin_0, J22.pin1
  N149: R27.Pin_0, J27.pin1
  N150: R29.Pin_0, J29.pin1
  N151: R25.Pin_0, J25.pin1
  N152: R28.Pin_0, J28.pin1
  N153: R26.Pin_0, J26.pin1
  N154: R30.Pin_0, J30.pin1
  N155: 1kR.Pin_0, npn.pin1
  N156: R31.Pin_0, J31.pin1
  N157: PinOut1.0, E_B_C.pin2
  N158: PinOut1.1, J2.pin2
  N159: PinOut1.2, J3.pin2
  N160: PinOut1.3, J4.pin2
  N161: PinOut1.4, J5.pin2
  N162: PinOut1.5, J6.pin2
  N163: PinOut1.6, J7.pin2
  N164: PinOut1.7, J8.pin2
  N165: PinOut2.0, J9.pin2
  N166: PinOut2.1, J10.pin2
  N167: PinOut2.2, J11.pin2
  N168: PinOut2.3, J12.pin2
  N169: PinOut2.4, J13.pin2
  N170: PinOut2.5, J14.pin2
  N171: PinOut2.6, J15.pin2
  N172: PinOut2.7, J16.pin2
  N173: PinOut3.0, J17.pin2
  N174: PinOut3.1, J18.pin2
  N175: PinOut3.2, J19.pin2
  N176: PinOut3.3, J20.pin2
  N177: PinOut3.4, J21.pin2
  N178: PinOut3.5, J22.pin2
  N179: PinOut3.6, J23.pin2
  N180: PinOut3.7, J24.pin2
  N181: PinOut4.0, J25.pin2
  N182: PinOut4.1, J26.pin2
  N183: PinOut4.2, J27.pin2
  N184: PinOut4.3, J28.pin2
  N185: PinOut4.4, J29.pin2
  N186: PinOut4.5, J30.pin2
  N187: PinOut4.6, J31.pin2
  N188: PinOut4.7, npn.pin2
  N189: PinIn2.0, R41.Pin_0, latch-3.Q4
  N190: PinIn2.1, R42.Pin_0, latch-3.Q6
  N191: PinIn2.2, R43.Pin_0, latch-3.DS
  N192: PinIn2.3, R44.Pin_0, latch-3.ST_CP

notes:
  For the on/off switch B0 will use its internal pull-up resistor und and will be pulled to GND when the switch is closed [On].
  The switches each have a separate 10k pull-down resistor and will need VCC as input.
  The visible labels for this mini-usb header are wrong! Where GND is seen, 5V are actually [as one can see by hovering the mouse over it.] and vice versa.

custom parts:
  atmega328p: Atmel ATmega328 microcontroller.
  74HC165: 8-bit parallel in, serial out shift register
  CD4043B: Quad 3-state S/R-Latches
  Capacitor: Capacitor Standard 0603 ceramic capacitor, and 0.1 leaded capacitor.
  Mini-USB _B_ connector with 5th pin broken out.: Mini-USB B connector with 5th pin broken out. Created new symbol breaking out 5th ID pin in mini/micro USB connector spec. See: http://en.wikipedia.org/wiki/Mini_usb#Cables. Uses same footprint as 4-pin symbol. Also added pins to connect to mounting / shield pads if required (probably not generally needed as signals aren't shielded once they leave the connector).
