# Fritzing sketch 202402_GameBoard_Rev2_fudged (saved by Fritzing 1.0.0d)
circuit board: 15.3765cm x 12.8456cm
breadboards: 1

parts:
  Quartz_16MHz = Crystal [frequency="16 Mhz" package=THT]
  Atmega328P = atmega328p [package=dip]
  Reset_10kR = Resistor [tolerance=±5% resistance=10k power=0.25W package=THT]
  SPI = AVR ISP 6 Pin [package=2x3_lock]
  SR-1 = 74HC595 [package="DIP16 [THT]"]
  Periph_10kR = Resistor [tolerance=±5% resistance=10k power=0.25W package=THT]
  SR-2 = 74HC595 [package="DIP16 [THT]"]
  SR-3 = 74HC595 [package="DIP16 [THT]"]
  SR-4 = 74HC595 [package="DIP16 [THT]"]
  pIn-1 = 74HC165 [package="DIP16 [THT]"]
  pIn-2 = 74HC165 [package="DIP16 [THT]"]
  pIn-3 = 74HC165 [package="DIP16 [THT]"]
  pIn-4 = 74HC165 [package="DIP16 [THT]"]
  latch-1 = CD4043B [package="DIP16 [THT]"]
  latch-2 = CD4043B [package="DIP16 [THT]"]
  latch-3 = CD4043B [package="DIP16 [THT]"]
  latch-4 = CD4043B [package="DIP16 [THT]"]
  latch-5 = CD4043B [package="DIP16 [THT]"]
  latch-6 = CD4043B [package="DIP16 [THT]"]
  latch-7 = CD4043B [package="DIP16 [THT]"]
  latch-8 = CD4043B [package="DIP16 [THT]"]
  R-OnOff_10kR = Resistor [tolerance=±5% resistance=10k power=0.25W package=THT]
  22nF = Capacitor [package=cap-pth-small2]
  22nF_2 = Capacitor [package=cap-pth-small2]
  R1 = Resistor [tolerance=±5% resistance=1k power=0.25W package=THT]
  Q1 = TRANSISTOR_NPN [part_number=2N2222A package=to-92-ammo]
  R2 = Resistor [tolerance=±5% resistance=1k power=0.25W package=THT]
  Q2 = TRANSISTOR_NPN [package=to-92-ammo]
  R3 = Resistor [tolerance=±5% resistance=1k power=0.25W package=THT]
  Q3 = TRANSISTOR_NPN [package=to-92-ammo]
  R4 = Resistor [tolerance=±5% resistance=1k power=0.25W package=THT]
  Q4 = TRANSISTOR_NPN [package=to-92-ammo]
  R5 = Resistor [tolerance=±5% resistance=1k power=0.25W package=THT]
  R6 = Resistor [tolerance=±5% resistance=1k power=0.25W package=THT]
  R7 = Resistor [tolerance=±5% resistance=1k power=0.25W package=THT]
  R8 = Resistor [tolerance=±5% resistance=1k power=0.25W package=THT]
  Q5 = TRANSISTOR_NPN [package=to-92-ammo]
  Q6 = TRANSISTOR_NPN [package=to-92-ammo]
  Q7 = TRANSISTOR_NPN [package=to-92-ammo]
  Q8 = TRANSISTOR_NPN [package=to-92-ammo]
  R9 = Resistor [tolerance=±5% resistance=1k power=0.25W package=THT]
  R10 = Resistor [tolerance=±5% resistance=1k power=0.25W package=THT]
  R11 = Resistor [tolerance=±5% resistance=1k power=0.25W package=THT]
  R12 = Resistor [tolerance=±5% resistance=1k power=0.25W package=THT]
  R13 = Resistor [tolerance=±5% resistance=1k power=0.25W package=THT]
  R14 = Resistor [tolerance=±5% resistance=1k power=0.25W package=THT]
  R15 = Resistor [tolerance=±5% resistance=1k power=0.25W package=THT]
  R16 = Resistor [tolerance=±5% resistance=1k power=0.25W package=THT]
  Q9 = TRANSISTOR_NPN [package=to-92-ammo]
  Q10 = TRANSISTOR_NPN [package=to-92-ammo]
  Q11 = TRANSISTOR_NPN [package=to-92-ammo]
  Q12 = TRANSISTOR_NPN [package=to-92-ammo]
  Q13 = TRANSISTOR_NPN [package=to-92-ammo]
  Q14 = TRANSISTOR_NPN [package=to-92-ammo]
  Q15 = TRANSISTOR_NPN [package=to-92-ammo]
  Q16 = TRANSISTOR_NPN [package=to-92-ammo]
  R17 = Resistor [tolerance=±5% resistance=1k power=0.25W package=THT]
  R18 = Resistor [tolerance=±5% resistance=1k power=0.25W package=THT]
  R19 = Resistor [tolerance=±5% resistance=1k power=0.25W package=THT]
  R20 = Resistor [tolerance=±5% resistance=1k power=0.25W package=THT]
  R21 = Resistor [tolerance=±5% resistance=1k power=0.25W package=THT]
  R22 = Resistor [tolerance=±5% resistance=1k power=0.25W package=THT]
  R23 = Resistor [tolerance=±5% resistance=1k power=0.25W package=THT]
  R24 = Resistor [tolerance=±5% resistance=1k power=0.25W package=THT]
  Q17 = TRANSISTOR_NPN [package=to-92-ammo]
  Q18 = TRANSISTOR_NPN [package=to-92-ammo]
  Q19 = TRANSISTOR_NPN [package=to-92-ammo]
  Q20 = TRANSISTOR_NPN [package=to-92-ammo]
  Q21 = TRANSISTOR_NPN [package=to-92-ammo]
  Q22 = TRANSISTOR_NPN [package=to-92-ammo]
  Q23 = TRANSISTOR_NPN [package=to-92-ammo]
  Q24 = TRANSISTOR_NPN [package=to-92-ammo]
  R25 = Resistor [tolerance=±5% resistance=1k power=0.25W package=THT]
  R26 = Resistor [tolerance=±5% resistance=1k power=0.25W package=THT]
  R27 = Resistor [tolerance=±5% resistance=1k power=0.25W package=THT]
  R28 = Resistor [tolerance=±5% resistance=1k power=0.25W package=THT]
  R29 = Resistor [tolerance=±5% resistance=1k power=0.25W package=THT]
  R30 = Resistor [tolerance=±5% resistance=1k power=0.25W package=THT]
  R31 = Resistor [tolerance=±5% resistance=1k power=0.25W package=THT]
  R32 = Resistor [tolerance=±5% resistance=1k power=0.25W package=THT]
  Q25 = TRANSISTOR_NPN [package=to-92-ammo]
  Q26 = TRANSISTOR_NPN [package=to-92-ammo]
  Q27 = TRANSISTOR_NPN [package=to-92-ammo]
  Q28 = TRANSISTOR_NPN [package=to-92-ammo]
  Q29 = TRANSISTOR_NPN [package=to-92-ammo]
  Q30 = TRANSISTOR_NPN [package=to-92-ammo]
  Q31 = TRANSISTOR_NPN [package=to-92-ammo]
  Q32 = TRANSISTOR_NPN [package=to-92-ammo]
  2N5401 = PNP-Transistor [part_number=2N5401 package="TO92 [THT]"]
  220µF = Electrolytic Capacitor [capacitance=0.22mF package="200 mil [THT, electrolytic]"]
  220µF_2 = Electrolytic Capacitor [capacitance=0.22mF package="200 mil [THT, electrolytic]"]
  Mini-USB = Mini-USB _B_ connector with 5th pin broken out. [package=usb-minib]
  R65 = Resistor [tolerance=±5% resistance=10k power=0.25W package=THT]
  R66 = Resistor [tolerance=±5% resistance=10k power=0.25W package=THT]
  R67 = Resistor [tolerance=±5% resistance=10k power=0.25W package=THT]
  R68 = Resistor [tolerance=±5% resistance=10k power=0.25W package=THT]
  R69 = Resistor [tolerance=±5% resistance=10k power=0.25W package=THT]
  R71 = Resistor [tolerance=±5% resistance=10k power=0.25W package=THT]
  R72 = Resistor [tolerance=±5% resistance=10k power=0.25W package=THT]
  R73 = Resistor [tolerance=±5% resistance=10k power=0.25W package=THT]
  R74 = Resistor [tolerance=±5% resistance=10k power=0.25W package=THT]
  R75 = Resistor [tolerance=±5% resistance=10k power=0.25W package=THT]
  R76 = Resistor [tolerance=±5% resistance=10k power=0.25W package=THT]
  R77 = Resistor [tolerance=±5% resistance=10k power=0.25W package=THT]
  R78 = Resistor [tolerance=±5% resistance=10k power=0.25W package=THT]
  R79 = Resistor [tolerance=±5% resistance=10k power=0.25W package=THT]
  R80 = Resistor [tolerance=±5% resistance=10k power=0.25W package=THT]
  R81 = Resistor [tolerance=±5% resistance=10k power=0.25W package=THT]
  R82 = Resistor [tolerance=±5% resistance=10k power=0.25W package=THT]
  R83 = Resistor [tolerance=±5% resistance=10k power=0.25W package=THT]
  R84 = Resistor [tolerance=±5% resistance=10k power=0.25W package=THT]
  R85 = Resistor [tolerance=±5% resistance=10k power=0.25W package=THT]
  R86 = Resistor [tolerance=±5% resistance=10k power=0.25W package=THT]
  R87 = Resistor [tolerance=±5% resistance=10k power=0.25W package=THT]
  R88 = Resistor [tolerance=±5% resistance=10k power=0.25W package=THT]
  R89 = Resistor [tolerance=±5% resistance=10k power=0.25W package=THT]
  R90 = Resistor [tolerance=±5% resistance=10k power=0.25W package=THT]
  R91 = Resistor [tolerance=±5% resistance=10k power=0.25W package=THT]
  R92 = Resistor [tolerance=±5% resistance=10k power=0.25W package=THT]
  R93 = Resistor [tolerance=±5% resistance=10k power=0.25W package=THT]
  R94 = Resistor [tolerance=±5% resistance=10k power=0.25W package=THT]
  R95 = Resistor [tolerance=±5% resistance=10k power=0.25W package=THT]
  R96 = Resistor [tolerance=±5% resistance=10k power=0.25W package=THT]
  q7 = female pin header, 1 pin [form="♀ (female)"]
  R70 = Resistor [tolerance=±5% resistance=10k power=0.25W package=THT]
  J1 = Generic female header - 8 pins [form="♀ (female)" package=THT]
  J2 = Generic female header - 8 pins [form="♀ (female)" package=THT]
  J3 = Generic female header - 8 pins [form="♀ (female)" package=THT]
  J4 = Generic female header - 8 pins [form="♀ (female)" package=THT]
  J5 = Generic female header - 8 pins [form="♀ (female)" package=THT]
  J6 = Generic female header - 8 pins [form="♀ (female)" package=THT]
  J7 = Generic female header - 8 pins [form="♀ (female)" package=THT]
  J8 = Generic female header - 8 pins [form="♀ (female)" package=THT]
  J9 = Generic female header - 8 pins [form="♀ (female)" package=THT]
  J10 = Generic female header - 8 pins [form="♀ (female)" package=THT]

nets:
  N1: Quartz_16MHz.pin_0, Atmega328P.B6_(XTAL1), 22nF.1
  N2: Quartz_16MHz.pin_1, Atmega328P.B7_(XTAL2), 22nF_2.1
  N3: Atmega328P.RESET, Reset_10kR.Pin_1, SPI.5
  N4: Atmega328P.D0_(RX), J5.D7
  N5: Atmega328P.D1_(TX), J5.D6
  N6: Atmega328P.D2, SR-1.DS
  N7: Atmega328P.D3_(PWM), SR-1.OE, SR-2.OE, SR-3.OE, SR-4.OE
  N8: Atmega328P.D4, SR-1.ST_CP, SR-2.ST_CP, SR-3.ST_CP, SR-4.ST_CP
  5V: Atmega328P.VCC, Atmega328P.AVCC, Atmega328P.AREF, Reset_10kR.Pin_0, SPI.2, 2N5401.E, 220µF.+, 220µF_2.+, Mini-USB.VBUS, J6.D0, J6.D1, J6.D6
  GND: Atmega328P.GND, SPI.6, SR-1.GND, SR-2.GND, SR-3.GND, SR-4.GND, pIn-1.GND, pIn-1.MR, pIn-1.Q0, pIn-2.GND, pIn-2.Q0, pIn-3.GND, pIn-3.Q0, pIn-4.GND, pIn-4.Q0, latch-1.GND, latch-2.GND, latch-3.GND, latch-4.GND, latch-5.GND, latch-6.GND, latch-7.GND, latch-8.GND, 22nF.2, 22nF_2.2, Q1.E, Q2.E, Q3.E, Q4.E, Q5.E, Q6.E, Q7.E, Q8.E, Q9.E, Q10.E, Q11.E, Q12.E, Q13.E, Q14.E, Q15.E, Q16.E, Q17.E, Q18.E, Q19.E, Q20.E, Q21.E, Q22.E, Q23.E, Q24.E, Q25.E, Q26.E, Q27.E, Q28.E, Q29.E, Q30.E, Q31.E, Q32.E, 220µF.-, 220µF_2.-, Mini-USB.MTN2, Mini-USB.MTN3, Mini-USB.MTN1, Mini-USB.MTN4, Mini-USB.GND, R65.Pin_1, R66.Pin_1, R67.Pin_1, R68.Pin_1, R69.Pin_1, R71.Pin_1, R72.Pin_1, R73.Pin_1, R74.Pin_1, R75.Pin_1, R76.Pin_1, R77.Pin_1, R78.Pin_1, R79.Pin_1, R80.Pin_1, R81.Pin_1, R82.Pin_1, R83.Pin_1, R84.Pin_1, R85.Pin_1, R86.Pin_1, R87.Pin_1, R88.Pin_1, R89.Pin_1, R90.Pin_1, R91.Pin_1, R92.Pin_1, R93.Pin_1, R94.Pin_1, R95.Pin_1, R96.Pin_1, R70.Pin_1, J5.D0, J5.D1, J5.D4, J6.D7
  N9: Atmega328P.D5_(PWM), SR-1.SH_CP, SR-2.SH_CP, SR-3.SH_CP, SR-4.SH_CP
  N10: Atmega328P.D6_(PWM), SR-1.MR, SR-2.MR, SR-3.MR, SR-4.MR
  N11: Atmega328P.D7, J6.D5
  N12: Atmega328P.B0, R-OnOff_10kR.Pin_1
  N13: Atmega328P.B1_(PWM), J6.D4
  N14: Atmega328P.B2_(PWM), J6.D3
  N15: Atmega328P.B3_(PWM), SPI.4
  N16: Atmega328P.B4, SPI.1
  N17: Atmega328P.B5, SPI.3
  N18: Atmega328P.C0, J6.D2
  N19: Atmega328P.C1, latch-1.Q3, latch-1.Q7, latch-1.SH_CP, latch-1.Q0, latch-2.Q3, latch-2.Q7, latch-2.SH_CP, latch-2.Q0, latch-3.Q3, latch-3.Q7, latch-3.SH_CP, latch-3.Q0, latch-4.Q3, latch-4.Q7, latch-4.SH_CP, latch-4.Q0, latch-5.Q3, latch-5.Q7, latch-5.SH_CP, latch-5.Q0, latch-6.Q3, latch-6.Q7, latch-6.SH_CP, latch-6.Q0, latch-7.Q3, latch-7.Q7, latch-7.SH_CP, latch-7.Q0, latch-8.Q3, latch-8.Q7, latch-8.SH_CP, latch-8.Q0
  N20: Atmega328P.C2, pIn-1.Q2, pIn-2.Q2, pIn-3.Q2, pIn-4.Q2
  N21: Atmega328P.C3, pIn-1.Q1, pIn-2.Q1, pIn-3.Q1, pIn-4.Q1
  N22: Atmega328P.C4, pIn-4.Q7'
  N23: Atmega328P.C5, Periph_10kR.Pin_0
  N24: SR-1.Q1, R2.Pin_1
  N25: SR-1.Q2, R3.Pin_1
  N26: SR-1.Q3, R4.Pin_1
  N27: SR-1.Q4, R5.Pin_1
  N28: SR-1.Q5, R8.Pin_1
  N29: SR-1.Q6, R7.Pin_1
  N30: SR-1.Q7, R6.Pin_1
  N31: SR-1.Q7', SR-2.DS
  N32: SR-1.Q0, R1.Pin_1
  VCC: SR-1.VCC, SR-2.VCC, SR-3.VCC, SR-4.VCC, pIn-1.VCC, pIn-2.VCC, pIn-3.VCC, pIn-4.VCC, latch-1.Q5, latch-1.VCC, latch-2.Q5, latch-2.VCC, latch-3.Q5, latch-3.VCC, latch-4.Q5, latch-4.VCC, latch-5.Q5, latch-5.VCC, latch-6.Q5, latch-6.VCC, latch-7.Q5, latch-7.VCC, latch-8.Q5, latch-8.VCC, 2N5401.C, J5.D2, J5.D3
  N33: Periph_10kR.Pin_1, 2N5401.B
  N34: SR-2.Q1, R15.Pin_1
  N35: SR-2.Q2, R11.Pin_1
  N36: SR-2.Q3, R16.Pin_1
  N37: SR-2.Q4, R10.Pin_1
  N38: SR-2.Q5, R14.Pin_1
  N39: SR-2.Q6, R12.Pin_1
  N40: SR-2.Q7, R13.Pin_1
  N41: SR-2.Q7', SR-3.DS
  N42: SR-2.Q0, R9.Pin_1
  N43: SR-3.Q1, R19.Pin_1
  N44: SR-3.Q2, R20.Pin_1
  N45: SR-3.Q3, R21.Pin_1
  N46: SR-3.Q4, R23.Pin_1
  N47: SR-3.Q5, R24.Pin_1
  N48: SR-3.Q6, R18.Pin_1
  N49: SR-3.Q7, R22.Pin_1
  N50: SR-3.Q7', SR-4.DS
  N51: SR-3.Q0, R17.Pin_1
  N52: SR-4.Q1, R29.Pin_1
  N53: SR-4.Q2, R25.Pin_1
  N54: SR-4.Q3, R28.Pin_1
  N55: SR-4.Q4, R26.Pin_1
  N56: SR-4.Q5, R30.Pin_1
  N57: SR-4.Q6, R32.Pin_1
  N58: SR-4.Q7, R31.Pin_1
  N59: SR-4.Q7', q7.pin1
  N60: SR-4.Q0, R27.Pin_1
  N61: pIn-1.Q3, latch-2.Q2
  N62: pIn-1.Q4, latch-2.Q7'
  N63: pIn-1.Q5, latch-2.Q1
  N64: pIn-1.Q6, latch-2.MR
  N65: pIn-1.Q7', pIn-2.MR
  N66: pIn-1.SH_CP, latch-1.Q2
  N67: pIn-1.ST_CP, latch-1.Q7'
  N68: pIn-1.OE, latch-1.Q1
  N69: pIn-1.DS, latch-1.MR
  N70: pIn-2.Q3, latch-4.Q2
  N71: pIn-2.Q4, latch-4.Q7'
  N72: pIn-2.Q5, latch-4.Q1
  N73: pIn-2.Q6, latch-4.MR
  N74: pIn-2.Q7', pIn-3.MR
  N75: pIn-2.SH_CP, latch-3.Q2
  N76: pIn-2.ST_CP, latch-3.Q7'
  N77: pIn-2.OE, latch-3.Q1
  N78: pIn-2.DS, latch-3.MR
  N79: pIn-3.Q3, latch-6.Q2
  N80: pIn-3.Q4, latch-6.Q7'
  N81: pIn-3.Q5, latch-6.Q1
  N82: pIn-3.Q6, latch-6.MR
  N83: pIn-3.Q7', pIn-4.MR
  N84: pIn-3.SH_CP, latch-5.Q2
  N85: pIn-3.ST_CP, latch-5.Q7'
  N86: pIn-3.OE, latch-5.Q1
  N87: pIn-3.DS, latch-5.MR
  N88: pIn-4.Q3, latch-8.Q2
  N89: pIn-4.Q4, latch-8.Q7'
  N90: pIn-4.Q5, latch-8.Q1
  N91: pIn-4.Q6, latch-8.MR
  N92: pIn-4.SH_CP, latch-7.Q2
  N93: pIn-4.ST_CP, latch-7.Q7'
  N94: pIn-4.OE, latch-7.Q1
  N95: pIn-4.DS, latch-7.MR
  N96: latch-1.Q4, R96.Pin_0, J7.D0
  N97: latch-1.Q6, R95.Pin_0, J7.D1
  N98: latch-1.ST_CP, R93.Pin_0, J7.D3
  N99: latch-1.DS, R94.Pin_0, J7.D2
  N100: latch-2.Q4, R92.Pin_0, J7.D4
  N101: latch-2.Q6, R90.Pin_0, J7.D5
  N102: latch-2.ST_CP, R91.Pin_0, J7.D7
  N103: latch-2.DS, R89.Pin_0, J7.D6
  N104: latch-3.Q4, R88.Pin_0, J8.D0
  N105: latch-3.Q6, R82.Pin_0, J8.D1
  N106: latch-3.ST_CP, R84.Pin_0, J8.D3
  N107: latch-3.DS, R83.Pin_0, J8.D2
  N108: latch-4.Q4, R87.Pin_0, J8.D4
  N109: latch-4.Q6, R81.Pin_0, J8.D5
  N110: latch-4.ST_CP, R86.Pin_0, J8.D7
  N111: latch-4.DS, R85.Pin_0, J8.D6
  N112: latch-5.Q4, R80.Pin_0, J9.D0
  N113: latch-5.Q6, R74.Pin_0, J9.D1
  N114: latch-5.ST_CP, R76.Pin_0, J9.D3
  N115: latch-5.DS, R75.Pin_0, J9.D2
  N116: latch-6.Q4, R79.Pin_0, J9.D4
  N117: latch-6.Q6, R73.Pin_0, J9.D5
  N118: latch-6.ST_CP, R78.Pin_0, J9.D7
  N119: latch-6.DS, R77.Pin_0, J9.D6
  N120: latch-7.Q4, R72.Pin_0, J10.D0
  N121: latch-7.Q6, R66.Pin_0, J10.D1
  N122: latch-7.ST_CP, R68.Pin_0, J10.D3
  N123: latch-7.DS, R67.Pin_0, J10.D2
  N124: latch-8.Q4, R71.Pin_0, J10.D4
  N125: latch-8.Q6, R65.Pin_0, J10.D5
  N126: latch-8.ST_CP, R70.Pin_0, J10.D7
  N127: latch-8.DS, R69.Pin_0, J10.D6
  N128: R-OnOff_10kR.Pin_0, J5.D5
  N129: R1.Pin_0, Q1.B
  N130: Q1.C, J1.D0
  N131: R2.Pin_0, Q2.B
  N132: Q2.C, J1.D1
  N133: R3.Pin_0, Q3.B
  N134: Q3.C, J1.D2
  N135: R4.Pin_0, Q4.B
  N136: Q4.C, J1.D3
  N137: R5.Pin_0, Q5.B
  N138: R6.Pin_0, Q8.B
  N139: R7.Pin_0, Q6.B
  N140: R8.Pin_0, Q7.B
  N141: Q5.C, J1.D4
  N142: Q6.C, J1.D6
  N143: Q7.C, J1.D5
  N144: Q8.C, J1.D7
  N145: R9.Pin_0, Q9.B
  N146: R10.Pin_0, Q10.B
  N147: R11.Pin_0, Q12.B
  N148: R12.Pin_0, Q14.B
  N149: R13.Pin_0, Q11.B
  N150: R14.Pin_0, Q16.B
  N151: R15.Pin_0, Q15.B
  N152: R16.Pin_0, Q13.B
  N153: Q9.C, J2.D0
  N154: Q10.C, J2.D4
  N155: Q11.C, J2.D7
  N156: Q12.C, J2.D2
  N157: Q13.C, J2.D3
  N158: Q14.C, J2.D6
  N159: Q15.C, J2.D1
  N160: Q16.C, J2.D5
  N161: R17.Pin_0, Q20.B
  N162: R18.Pin_0, Q23.B
  N163: R19.Pin_0, Q22.B
  N164: R20.Pin_0, Q18.B
  N165: R21.Pin_0, Q17.B
  N166: R22.Pin_0, Q19.B
  N167: R23.Pin_0, Q21.B
  N168: R24.Pin_0, Q24.B
  N169: Q17.C, J3.D3
  N170: Q18.C, J3.D2
  N171: Q19.C, J3.D7
  N172: Q20.C, J3.D0
  N173: Q21.C, J3.D4
  N174: Q22.C, J3.D1
  N175: Q23.C, J3.D6
  N176: Q24.C, J3.D5
  N177: R25.Pin_0, Q30.B
  N178: R26.Pin_0, Q29.B
  N179: R27.Pin_0, Q28.B
  N180: R28.Pin_0, Q31.B
  N181: R29.Pin_0, Q32.B
  N182: R30.Pin_0, Q26.B
  N183: R31.Pin_0, Q27.B
  N184: R32.Pin_0, Q25.B
  N185: Q25.C, J4.D6
  N186: Q26.C, J4.D5
  N187: Q27.C, J4.D7
  N188: Q28.C, J4.D0
  N189: Q29.C, J4.D4
  N190: Q30.C, J4.D2
  N191: Q31.C, J4.D3
  N192: Q32.C, J4.D1

notes:
  GND
  VCC
  In31
  10kR
  In0
  VCCo
  D7
  B1
  B2
  C0
  MOSI
  MISO
  CLK
  Reset
  Sw.OnOff-
  D0
  D1
  Sw.OnOff+
  In8
  In16
  In24
  CD4043B
  74HC165
  R1
  S1
  OE
  S0
  Q3
  R0
  Q0
  Q1
  Q2
  S2
  R3
  S3
  R2
  NC
  CP
  D5
  nPL
  D6
  D4
  nd7
  SER
  d7
  D2
  nCE
  D3
  74HC595
  nOE
  RCLK
  SRCLK
  nSRCLR
  q7
  B3 (MOSI)
  B4 (MISO)
  B5 (CLK)
  Out31
  Out0
  Out8
  Out16
  Out24
  C5
  C4
  C3
  C2
  C1
  B0
  nReset
  (RX) D0
  (TX) D1
  2N2222A
  E
  B
  C
  Button Matrix
  © Johannes Wilde
  Revision 2, February 2024

custom parts:
  atmega328p: Atmel ATmega328 microcontroller.
  74HC165: 8-bit parallel in, serial out shift register
  CD4043B: Quad 3-state S/R-Latches
  Capacitor: Capacitor Standard 0603 ceramic capacitor, and 0.1 leaded capacitor.
  Mini-USB _B_ connector with 5th pin broken out.: Mini-USB B connector with 5th pin broken out. Created new symbol breaking out 5th ID pin in mini/micro USB connector spec. See: http://en.wikipedia.org/wiki/Mini_usb#Cables. Uses same footprint as 4-pin symbol. Also added pins to connect to mounting / shield pads if required (probably not generally needed as signals aren't shielded once they leave the connector).
  Generic female header - 8 pins: Generic female header
